// Logisim project DeMorgan1_NOR.circ as structural Verilog: 3 circuits, main circuit DeMorgan
module main (
  input  B,
  input  A,
  output Y
);

  wire nand_1_out, nand_2_out, nand_3_out;

  nand nand_1 (nand_1_out, B, A);
  nand nand_2 (nand_2_out, B, nand_1_out);
  nand nand_3 (nand_3_out, nand_1_out, A);
  nand nand_4 (Y, nand_2_out, nand_3_out);
endmodule

module NANDtoNOR (
  input  A,
  input  B,
  input  C,
  input  D,
  output Y,
  output X
);

  wire nand_1_out, nand_2_out, nand_3_out, not_1_out, not_2_out;

  not not_1 (not_1_out, C);
  not not_2 (not_2_out, D);
  nand nand_1 (nand_1_out, A, A);
  nand nand_2 (nand_2_out, B, B);
  and and_1 (X, not_1_out, not_2_out);
  nand nand_3 (nand_3_out, nand_1_out, nand_2_out);
  nand nand_4 (Y, nand_3_out, nand_3_out);
endmodule

module DeMorgan (
  input  A,
  input  B,
  output Y2,
  output Y1
);

  wire nand_1_out, nand_2_out, nand_3_out, not_1_out, not_2_out;

  not not_1 (not_1_out, A);
  not not_2 (not_2_out, B);
  nand nand_1 (nand_1_out, A, A);
  and and_1 (Y2, not_1_out, not_2_out);
  nand nand_2 (nand_2_out, B, B);
  nand nand_3 (nand_3_out, nand_1_out, nand_2_out);
  nand nand_4 (Y1, nand_3_out, nand_3_out);
endmodule
