// Logisim project DeMorgan2_NAND.circ as structural Verilog: 2 circuits, main circuit DeMorgan2
module main (
  input  B,
  input  A,
  output Y
);

  wire and_1_out, and_2_out, and_3_out, and_4_out, P_out, Q_out, T_out;

  and and_1 (and_1_out, B, A);
  not T (T_out, and_1_out);
  buf and_2 (and_2_out, T_out);  // AND_Gate
  not P (P_out, and_3_out);
  buf and_3 (and_3_out, T_out);  // AND_Gate
  not Q (Q_out, and_2_out);
  buf and_4 (and_4_out, Q_out);  // AND_Gate
  not not_1 (Y, and_4_out);
endmodule

module DeMorgan2 (
  input  A,
  input  B,
  output Y2,
  output Y1
);

  wire not_1_out, not_2_out;

  not not_1 (not_1_out, A);
  not not_2 (not_2_out, B);
  or or_1 (Y2, not_1_out, not_2_out);
  nand nand_1 (Y1, A, B);
endmodule
