// Logisim project NandToNOR.circ as structural Verilog: 2 circuits, main circuit main
module main (
  input  B,
  input  A,
  output Y
);

  wire nand_1_out, nand_2_out, nand_3_out;

  nand nand_1 (nand_1_out, B, A);
  nand nand_2 (nand_2_out, B, nand_1_out);
  nand nand_3 (nand_3_out, nand_1_out, A);
  nand nand_4 (Y, nand_2_out, nand_3_out);
endmodule

module NANDtoNOR (
  input  A,
  input  B,
  output out_3
);

  wire nand_1_out, nand_2_out, nand_3_out;

  nand nand_1 (nand_1_out, A, A);
  nand nand_2 (nand_2_out, B, B);
  nand nand_3 (nand_3_out, nand_1_out, nand_2_out);
  nand nand_4 (out_3, nand_3_out, nand_3_out);
endmodule
