// Digital circuit decoder3_gatter.dig as structural Verilog
module decoder3_gatter (
  input  A2,
  input  A1,
  input  A0,
  output Y0,
  output Y1,
  output Y2,
  output Y3,
  output Y4,
  output Y5,
  output Y6,
  output Y7
);

  wire not_1_out, not_2_out, not_3_out;

  not not_1 (not_1_out, A2);
  not not_2 (not_2_out, A1);
  not not_3 (not_3_out, A0);
  and and_1 (Y0, not_1_out, not_2_out, not_3_out);
  and and_2 (Y1, not_1_out, not_2_out, A0);
  and and_3 (Y2, not_1_out, A1, not_3_out);
  and and_4 (Y3, not_1_out, A1, A0);
  and and_5 (Y4, A2, not_2_out, not_3_out);
  and and_6 (Y5, A2, not_2_out, A0);
  and and_7 (Y6, A2, A1, not_3_out);
  and and_8 (Y7, A2, A1, A0);
endmodule

/* Test case Full truth table:
A2 A1 A0 Y0 Y1 Y2 Y3 Y4 Y5 Y6 Y7
0 0 0 1 0 0 0 0 0 0 0
0 0 1 0 1 0 0 0 0 0 0
0 1 0 0 0 1 0 0 0 0 0
0 1 1 0 0 0 1 0 0 0 0
1 0 0 0 0 0 0 1 0 0 0
1 0 1 0 0 0 0 0 1 0 0
1 1 0 0 0 0 0 0 0 1 0
1 1 1 0 0 0 0 0 0 0 1
*/
