// Digital circuit majority3_mux.dig as structural Verilog
module majority3_mux (
  input  S0,
  input  S1,
  input  S2,
  output Y
);

  Multiplexer #(.Selector_Bits(3)) multiplexer_1 (
    .sel({S2, S1, S0}), .in_0(1'b1), .in_1(1'b1), .in_2(1'b1), .in_3(1'b0), .in_4(1'b1), .in_5(1'b0),
    .in_6(1'b0), .in_7(1'b0), .out(Y));
endmodule

/* Test case Full truth table:
S2 S1 S0 Y
0 0 0 0
0 0 1 0
0 1 0 0
0 1 1 1
1 0 0 0
1 0 1 1
1 1 0 1
1 1 1 1
*/
