// Digital circuit mux2to1.dig as structural Verilog
module mux2to1 (
  input  D0,
  input  S,
  input  D1,
  output Y
);

  wire and_1_out, and_2_out, not_1_out;

  not not_1 (not_1_out, S);
  and and_1 (and_1_out, D0, not_1_out);
  and and_2 (and_2_out, S, D1);
  or or_1 (Y, and_1_out, and_2_out);
endmodule

/* Test case MUX-Test:
S D0 D1 Y
0  0  0  0
0  0  1  0
0  1  0  1
0  1  1  1
1  0  0  0
1  0  1  1
1  1  0  0
1  1  1  1
*/
