// Digital circuit priority8_gatter.dig as structural Verilog
module priority8_gatter (
  input  I7,
  input  I6,
  input  I5,
  input  I4,
  input  I3,
  input  I2,
  input  I1,
  input  I0,
  output G7,
  output G6,
  output G5,
  output G4,
  output G3,
  output G2,
  output G1,
  output G0,
  output Q2,
  output Q1,
  output Q0,
  output NONE
);

  wire not_1_out, not_2_out, not_3_out, not_4_out, not_5_out, not_6_out, not_7_out;

  nor nor_1 (NONE, I0, I1, I2, I3, I4, I5, I6, I7);
  not not_1 (not_1_out, I1);
  not not_2 (not_2_out, I4);
  not not_3 (not_3_out, I3);
  not not_4 (not_4_out, I2);
  not not_5 (not_5_out, I6);
  not not_6 (not_6_out, I5);
  not not_7 (not_7_out, I7);
  and and_1 (G6, not_7_out, I6);
  and and_2 (G5, not_7_out, not_5_out, I5);
  and and_3 (G4, not_7_out, not_5_out, not_6_out, I4);
  and and_4 (G3, not_7_out, not_5_out, not_6_out, not_2_out, I3);
  and and_5 (G2, not_7_out, not_5_out, not_6_out, not_2_out, not_3_out, I2);
  and and_6 (G1, not_7_out, not_5_out, not_6_out, not_2_out, not_3_out, not_4_out, I1);
  and and_7 (G0, not_7_out, not_5_out, not_6_out, not_2_out, not_3_out, not_4_out, not_1_out, I0);
  or or_1 (Q2, I7, G6, G5, G4);
  or or_2 (Q1, I7, G6, G3, G2);
  or or_3 (Q0, I7, G5, G3, G1);

  assign G7 = I7;
endmodule

/* Test case Encoder:
I7 I6 I5 I4 I3 I2 I1 I0 Q2 Q1 Q0 NONE
0 0 0 0 0 0 0 0 0 0 0 1
0 0 0 0 0 0 0 1 0 0 0 0
0 0 0 0 0 0 1 0 0 0 1 0
0 0 0 0 0 0 1 1 0 0 1 0
0 0 0 0 0 1 0 0 0 1 0 0
0 0 0 0 0 1 0 1 0 1 0 0
0 0 0 0 0 1 1 0 0 1 0 0
0 0 0 0 0 1 1 1 0 1 0 0
0 0 0 0 1 0 0 0 0 1 1 0
0 0 0 0 1 0 0 1 0 1 1 0
0 0 0 0 1 0 1 0 0 1 1 0
0 0 0 0 1 0 1 1 0 1 1 0
0 0 0 0 1 1 0 0 0 1 1 0
0 0 0 0 1 1 0 1 0 1 1 0
0 0 0 0 1 1 1 0 0 1 1 0
0 0 0 0 1 1 1 1 0 1 1 0
0 0 0 1 0 0 0 0 1 0 0 0
0 0 0 1 0 0 0 1 1 0 0 0
0 0 0 1 0 0 1 0 1 0 0 0
0 0 0 1 0 0 1 1 1 0 0 0
0 0 0 1 0 1 0 0 1 0 0 0
0 0 0 1 0 1 0 1 1 0 0 0
0 0 0 1 0 1 1 0 1 0 0 0
0 0 0 1 0 1 1 1 1 0 0 0
0 0 0 1 1 0 0 0 1 0 0 0
0 0 0 1 1 0 0 1 1 0 0 0
0 0 0 1 1 0 1 0 1 0 0 0
0 0 0 1 1 0 1 1 1 0 0 0
0 0 0 1 1 1 0 0 1 0 0 0
0 0 0 1 1 1 0 1 1 0 0 0
0 0 0 1 1 1 1 0 1 0 0 0
0 0 0 1 1 1 1 1 1 0 0 0
0 0 1 0 0 0 0 0 1 0 1 0
0 0 1 0 0 0 0 1 1 0 1 0
0 0 1 0 0 0 1 0 1 0 1 0
0 0 1 0 0 0 1 1 1 0 1 0
0 0 1 0 0 1 0 0 1 0 1 0
0 0 1 0 0 1 0 1 1 0 1 0
0 0 1 0 0 1 1 0 1 0 1 0
0 0 1 0 0 1 1 1 1 0 1 0
0 0 1 0 1 0 0 0 1 0 1 0
0 0 1 0 1 0 0 1 1 0 1 0
0 0 1 0 1 0 1 0 1 0 1 0
0 0 1 0 1 0 1 1 1 0 1 0
0 0 1 0 1 1 0 0 1 0 1 0
0 0 1 0 1 1 0 1 1 0 1 0
0 0 1 0 1 1 1 0 1 0 1 0
0 0 1 0 1 1 1 1 1 0 1 0
0 0 1 1 0 0 0 0 1 0 1 0
0 0 1 1 0 0 0 1 1 0 1 0
0 0 1 1 0 0 1 0 1 0 1 0
0 0 1 1 0 0 1 1 1 0 1 0
0 0 1 1 0 1 0 0 1 0 1 0
0 0 1 1 0 1 0 1 1 0 1 0
0 0 1 1 0 1 1 0 1 0 1 0
0 0 1 1 0 1 1 1 1 0 1 0
0 0 1 1 1 0 0 0 1 0 1 0
0 0 1 1 1 0 0 1 1 0 1 0
0 0 1 1 1 0 1 0 1 0 1 0
0 0 1 1 1 0 1 1 1 0 1 0
0 0 1 1 1 1 0 0 1 0 1 0
0 0 1 1 1 1 0 1 1 0 1 0
0 0 1 1 1 1 1 0 1 0 1 0
0 0 1 1 1 1 1 1 1 0 1 0
0 1 0 0 0 0 0 0 1 1 0 0
0 1 0 0 0 0 0 1 1 1 0 0
0 1 0 0 0 0 1 0 1 1 0 0
0 1 0 0 0 0 1 1 1 1 0 0
0 1 0 0 0 1 0 0 1 1 0 0
0 1 0 0 0 1 0 1 1 1 0 0
0 1 0 0 0 1 1 0 1 1 0 0
0 1 0 0 0 1 1 1 1 1 0 0
0 1 0 0 1 0 0 0 1 1 0 0
0 1 0 0 1 0 0 1 1 1 0 0
0 1 0 0 1 0 1 0 1 1 0 0
0 1 0 0 1 0 1 1 1 1 0 0
0 1 0 0 1 1 0 0 1 1 0 0
0 1 0 0 1 1 0 1 1 1 0 0
0 1 0 0 1 1 1 0 1 1 0 0
0 1 0 0 1 1 1 1 1 1 0 0
0 1 0 1 0 0 0 0 1 1 0 0
0 1 0 1 0 0 0 1 1 1 0 0
0 1 0 1 0 0 1 0 1 1 0 0
0 1 0 1 0 0 1 1 1 1 0 0
0 1 0 1 0 1 0 0 1 1 0 0
0 1 0 1 0 1 0 1 1 1 0 0
0 1 0 1 0 1 1 0 1 1 0 0
0 1 0 1 0 1 1 1 1 1 0 0
0 1 0 1 1 0 0 0 1 1 0 0
0 1 0 1 1 0 0 1 1 1 0 0
0 1 0 1 1 0 1 0 1 1 0 0
0 1 0 1 1 0 1 1 1 1 0 0
0 1 0 1 1 1 0 0 1 1 0 0
0 1 0 1 1 1 0 1 1 1 0 0
0 1 0 1 1 1 1 0 1 1 0 0
0 1 0 1 1 1 1 1 1 1 0 0
0 1 1 0 0 0 0 0 1 1 0 0
0 1 1 0 0 0 0 1 1 1 0 0
0 1 1 0 0 0 1 0 1 1 0 0
0 1 1 0 0 0 1 1 1 1 0 0
0 1 1 0 0 1 0 0 1 1 0 0
0 1 1 0 0 1 0 1 1 1 0 0
0 1 1 0 0 1 1 0 1 1 0 0
0 1 1 0 0 1 1 1 1 1 0 0
0 1 1 0 1 0 0 0 1 1 0 0
0 1 1 0 1 0 0 1 1 1 0 0
0 1 1 0 1 0 1 0 1 1 0 0
0 1 1 0 1 0 1 1 1 1 0 0
0 1 1 0 1 1 0 0 1 1 0 0
0 1 1 0 1 1 0 1 1 1 0 0
0 1 1 0 1 1 1 0 1 1 0 0
0 1 1 0 1 1 1 1 1 1 0 0
0 1 1 1 0 0 0 0 1 1 0 0
0 1 1 1 0 0 0 1 1 1 0 0
0 1 1 1 0 0 1 0 1 1 0 0
0 1 1 1 0 0 1 1 1 1 0 0
0 1 1 1 0 1 0 0 1 1 0 0
0 1 1 1 0 1 0 1 1 1 0 0
0 1 1 1 0 1 1 0 1 1 0 0
0 1 1 1 0 1 1 1 1 1 0 0
0 1 1 1 1 0 0 0 1 1 0 0
0 1 1 1 1 0 0 1 1 1 0 0
0 1 1 1 1 0 1 0 1 1 0 0
0 1 1 1 1 0 1 1 1 1 0 0
0 1 1 1 1 1 0 0 1 1 0 0
0 1 1 1 1 1 0 1 1 1 0 0
0 1 1 1 1 1 1 0 1 1 0 0
0 1 1 1 1 1 1 1 1 1 0 0
1 0 0 0 0 0 0 0 1 1 1 0
1 0 0 0 0 0 0 1 1 1 1 0
1 0 0 0 0 0 1 0 1 1 1 0
1 0 0 0 0 0 1 1 1 1 1 0
1 0 0 0 0 1 0 0 1 1 1 0
1 0 0 0 0 1 0 1 1 1 1 0
1 0 0 0 0 1 1 0 1 1 1 0
1 0 0 0 0 1 1 1 1 1 1 0
1 0 0 0 1 0 0 0 1 1 1 0
1 0 0 0 1 0 0 1 1 1 1 0
1 0 0 0 1 0 1 0 1 1 1 0
1 0 0 0 1 0 1 1 1 1 1 0
1 0 0 0 1 1 0 0 1 1 1 0
1 0 0 0 1 1 0 1 1 1 1 0
1 0 0 0 1 1 1 0 1 1 1 0
1 0 0 0 1 1 1 1 1 1 1 0
1 0 0 1 0 0 0 0 1 1 1 0
1 0 0 1 0 0 0 1 1 1 1 0
1 0 0 1 0 0 1 0 1 1 1 0
1 0 0 1 0 0 1 1 1 1 1 0
1 0 0 1 0 1 0 0 1 1 1 0
1 0 0 1 0 1 0 1 1 1 1 0
1 0 0 1 0 1 1 0 1 1 1 0
1 0 0 1 0 1 1 1 1 1 1 0
1 0 0 1 1 0 0 0 1 1 1 0
1 0 0 1 1 0 0 1 1 1 1 0
1 0 0 1 1 0 1 0 1 1 1 0
1 0 0 1 1 0 1 1 1 1 1 0
1 0 0 1 1 1 0 0 1 1 1 0
1 0 0 1 1 1 0 1 1 1 1 0
1 0 0 1 1 1 1 0 1 1 1 0
1 0 0 1 1 1 1 1 1 1 1 0
1 0 1 0 0 0 0 0 1 1 1 0
1 0 1 0 0 0 0 1 1 1 1 0
1 0 1 0 0 0 1 0 1 1 1 0
1 0 1 0 0 0 1 1 1 1 1 0
1 0 1 0 0 1 0 0 1 1 1 0
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*/
