// Digital circuit 4d.dig as structural Verilog
module _4d (
  input  A,
  input  B,
  input  C,
  output Y
);

  wire and_1_out, and_2_out, and_3_out, not_1_out;

  not not_1 (not_1_out, A);
  and and_1 (and_1_out, A, B);
  and and_2 (and_2_out, not_1_out, C);
  and and_3 (and_3_out, C, B);
  or or_1 (Y, and_1_out, and_2_out, and_3_out);
endmodule
