// Digital circuit Gen_Prop.dig as structural Verilog
module Gen_Prop (
  input  A_i,
  input  B_i,
  input  C_i,
  output c_i_plus_1
);

  wire and_1_out, and_2_out, or_1_out;

  and and_1 (and_1_out, A_i, B_i);
  or or_1 (or_1_out, B_i, A_i);
  and and_2 (and_2_out, or_1_out, C_i);
  or or_2 (c_i_plus_1, and_1_out, and_2_out);
endmodule
