// Digital circuit adder.dig as structural Verilog
module adder (
  input  A,
  input  B,
  input  A1,
  input  B1,
  input  X,
  input  C_in,
  input  A2,
  input  C2,
  input  B2,
  input  C_in_2,
  output S,
  output C_out,
  output C_out1,
  output E
);

  wire and_1_out, and_2_out, and_3_out, and_4_out, and_5_out, xor_1_out, xor_2_out;

  xor xor_1 (xor_1_out, B2, C2);
  xor xor_2 (xor_2_out, A, B);
  and and_1 (and_1_out, A1, B1);
  and and_2 (and_2_out, X, C_in);
  xor xor_3 (E, A2, xor_1_out);
  and and_3 (and_3_out, A2, B2);
  and and_4 (and_4_out, A2, C2);
  and and_5 (and_5_out, B2, C2);
  xor xor_4 (S, C_in_2, xor_2_out);
  or or_1 (C_out, and_1_out, and_2_out);
  or or_2 (C_out1, and_3_out, and_4_out, and_5_out);
endmodule
