// Digital circuit Lookahead_Vergleich_8bit.dig as structural Verilog
// Referenzdemo: drei Wege berechnen denselben finalen Carry C8. Keine Summenbits. Alle Grundgatter haben 10 ns Laufzeit.
module Lookahead_Vergleich_8bit (
  input  A0,
  input  B0,
  input  A1,
  input  B1,
  input  A2,
  input  B2,
  input  A3,
  input  B3,
  input  A4,
  input  B4,
  input  A5,
  input  B5,
  input  A6,
  input  B6,
  input  A7,
  input  B7,
  input  Cin,
  output C8_Ripple,
  output C8_Block,
  output C8_Gruppe
);

  wire Bits_3_bis_0_cout, G0, G1, G1_0, G2, G3, G3_0, G3_2, G4, G5, G5_4, G6, G7, G7_0, G7_4, G7_6, P0, P1,
       P1_0, P2, P3, P3_0, P3_2, P4, P5, P5_4, P6, P7, P7_0, P7_4, P7_6, R0_cout, R1_cout, R2_cout, R3_cout,
       R4_cout, R5_cout, R6_cout;

  bit_gp Bit0 (.A(A0), .B(B0), .G(G0), .P(P0));
  carry_stufe R0 (.G(G0), .P(P0), .Cin(Cin), .Cout(R0_cout));
  gruppe_verbinden Bits_1_bis_0 (.GH(G1), .PH(P1), .GL(G0), .PL(P0), .G(G1_0), .P(P1_0));
  bit_gp Bit1 (.A(A1), .B(B1), .G(G1), .P(P1));
  carry_stufe R1 (.G(G1), .P(P1), .Cin(R0_cout), .Cout(R1_cout));
  block4_carry Bits_3_bis_0 (
    .G3(G3), .P3(P3), .G2(G2), .P2(P2), .G1(G1), .P1(P1), .G0(G0), .P0(P0), .Cin(Cin),
    .Cout(Bits_3_bis_0_cout));
  // Probe G_1_0 on G1_0
  gruppe_verbinden Bits_3_bis_0_2 (.GH(G3_2), .PH(P3_2), .GL(G1_0), .PL(P1_0), .G(G3_0), .P(P3_0));
  gruppe_verbinden Bits_3_bis_2 (.GH(G3), .PH(P3), .GL(G2), .PL(P2), .G(G3_2), .P(P3_2));
  // Probe G_3_0 on G3_0
  bit_gp Bit2 (.A(A2), .B(B2), .G(G2), .P(P2));
  carry_stufe R2 (.G(G2), .P(P2), .Cin(R1_cout), .Cout(R2_cout));
  gruppe_verbinden Bits_7_bis_0 (.GH(G7_4), .PH(P7_4), .GL(G3_0), .PL(P3_0), .G(G7_0), .P(P7_0));
  bit_gp Bit3 (.A(A3), .B(B3), .G(G3), .P(P3));
  carry_stufe R3 (.G(G3), .P(P3), .Cin(R2_cout), .Cout(R3_cout));
  // Probe G_7_0 on G7_0
  block4_carry Bits_7_bis_4 (
    .G3(G7), .P3(P7), .G2(G6), .P2(P6), .G1(G5), .P1(P5), .G0(G4), .P0(P4), .Cin(Bits_3_bis_0_cout),
    .Cout(C8_Block));
  gruppe_verbinden Bits_5_bis_4 (.GH(G5), .PH(P5), .GL(G4), .PL(P4), .G(G5_4), .P(P5_4));
  bit_gp Bit4 (.A(A4), .B(B4), .G(G4), .P(P4));
  carry_stufe R4 (.G(G4), .P(P4), .Cin(R3_cout), .Cout(R4_cout));
  gruppe_verbinden Bits_7_bis_4_2 (.GH(G7_6), .PH(P7_6), .GL(G5_4), .PL(P5_4), .G(G7_4), .P(P7_4));
  carry_stufe LetzterCarry (.G(G7_0), .P(P7_0), .Cin(Cin), .Cout(C8_Gruppe));
  bit_gp Bit5 (.A(A5), .B(B5), .G(G5), .P(P5));
  carry_stufe R5 (.G(G5), .P(P5), .Cin(R4_cout), .Cout(R5_cout));
  gruppe_verbinden Bits_7_bis_6 (.GH(G7), .PH(P7), .GL(G6), .PL(P6), .G(G7_6), .P(P7_6));
  bit_gp Bit6 (.A(A6), .B(B6), .G(G6), .P(P6));
  carry_stufe R6 (.G(G6), .P(P6), .Cin(R5_cout), .Cout(R6_cout));
  bit_gp Bit7 (.A(A7), .B(B7), .G(G7), .P(P7));
  carry_stufe R7 (.G(G7), .P(P7), .Cin(R6_cout), .Cout(C8_Ripple));

  // Notes on the sheet:
  //   B0: default 1
  //   A1: default 1
  //   A2: default 1
  //   A3: default 1
  //   A4: default 1
  //   A5: default 1
  //   A6: default 1
  //   A7: default 1
  //   Carry verstehen: Kette, feste Vier-Bit-Bloecke, Gruppenhierarchie
  //   Alle drei Wege bekommen dieselben A/B-Bits und denselben Cin. Beobachtet wird nur der letzte Carry C8.
  //   Start: A = 11111110, B = 00000001, Cin = 0. Schalte zum ersten Versuch nur A0 auf 1.
  //   Oben: Jede Bitstelle liefert G = A AND B und P = A OR B. Gleiche Tunnelnamen verbinden dieselbe Leitung.
  //   1. Ripple: acht Carry-Stufen hintereinander
  //   2. Block-Lookahead: zwei feste Vier-Bit-Bloecke; Carry von Block zu Block
  //   3. Hierarchie: Carry-Eigenschaften in Gruppen mit 2, dann 4, dann 8 Bits
  //   Die Gruppen warten auf ihre G/P-Informationen, nicht auf den Carry der vorherigen Bitstelle.
  //   Gruppenstufe 1: je zwei Bits
  //   Gruppenstufe 2: je vier Bits
  //   Gruppenstufe 3: alle acht Bits
  //   Im Graphen: A0 oder Cin umschalten; C8_Ripple, C8_Block und C8_Gruppe vergleichen.
  //   Die Zeiten gehoeren zu diesem 10-ns-Gattermodell. Die Demo berechnet C8; fuer alle Summen braucht man weitere Carry-Ausgaenge.
endmodule
