// Digital circuit bit_gp.dig as structural Verilog
// Eine Bitstelle: G = A AND B; P = A OR B.
module bit_gp (
  input  A,
  input  B,
  output G,
  output P
);

  and and_1 (G, A, B);
  or or_1 (P, B, A);

  // Notes on the sheet:
  //   Generate und Propagate fuer eine Bitstelle
  //   G = A AND B
  //   P = A OR B
endmodule
