// Digital circuit block4_carry.dig as structural Verilog
// Fester Vier-Bit-Block: G/P werden fuer vier Bits vorab gebildet. Cout = G_3_0 OR (P_3_0 AND Cin).
module block4_carry (
  input  G3,
  input  P3,
  input  G2,
  input  P2,
  input  G1,
  input  P1,
  input  G0,
  input  P0,
  input  Cin,
  output Cout
);

  wire G1_0, G3_0, G3_2, P1_0, P3_0, P3_2;

  gruppe_verbinden Bits1_0 (.GH(G1), .PH(P1), .GL(G0), .PL(P0), .G(G1_0), .P(P1_0));
  gruppe_verbinden Bits3_0 (.GH(G3_2), .PH(P3_2), .GL(G1_0), .PL(P1_0), .G(G3_0), .P(P3_0));
  gruppe_verbinden Bits3_2 (.GH(G3), .PH(P3), .GL(G2), .PL(P2), .G(G3_2), .P(P3_2));
  carry_stufe BlockCarry (.G(G3_0), .P(P3_0), .Cin(Cin), .Cout(Cout));

  // Notes on the sheet:
  //   Fester Vier-Bit-Lookahead-Block
  //   Intern werden Carry-Eigenschaften parallel zusammengefasst.
  //   Der kommende Block wartet trotzdem auf diesen Carry-Ausgang.
endmodule
