// Digital circuit carry_stufe.dig as structural Verilog
// Carry-Ausgang = G OR (P AND Cin).
module carry_stufe (
  input  G,
  input  P,
  input  Cin,
  output Cout
);

  wire and_1_out;

  and and_1 (and_1_out, P, Cin);
  or or_1 (Cout, G, and_1_out);

  // Notes on the sheet:
  //   Eine Carry-Stufe: Cout = G OR (P AND Cin)
endmodule
