// Digital circuit gruppe_verbinden.dig as structural Verilog
// H = hoeherer Abschnitt, L = niedrigerer Abschnitt. G = GH OR (PH AND GL); P = PH AND PL.
module gruppe_verbinden (
  input  GH,
  input  PH,
  input  GL,
  input  PL,
  output G,
  output P
);

  wire and_1_out;

  and and_1 (and_1_out, PH, GL);
  and and_2 (P, PH, PL);
  or or_1 (G, GH, and_1_out);

  // Notes on the sheet:
  //   Zwei benachbarte Abschnitte zu einer Gruppe verbinden
  //   G = GH OR (PH AND GL)
  //   P = PH AND PL
endmodule
