// Digital circuit ripple4.dig as structural Verilog
module ripple4 (
  input  C_in,
  input  B0,
  input  A0,
  input  A1,
  input  B1,
  input  A2,
  input  B2,
  input  A3,
  input  B3,
  output S0,
  output S1,
  output S2,
  output S3,
  output C_out
);

  wire FA0_c_o, FA1_c_o, FA2_c_o;

  Add FA0 (.a(A0), .b(B0), .c_i(C_in), .s(S0), .c_o(FA0_c_o));
  Add FA1 (.a(A1), .b(B1), .c_i(FA0_c_o), .s(S1), .c_o(FA1_c_o));
  Add FA2 (.a(A2), .b(B2), .c_i(FA1_c_o), .s(S2), .c_o(FA2_c_o));
  Add FA3 (.a(A3), .b(B3), .c_i(FA2_c_o), .s(S3), .c_o(C_out));
endmodule
